// Logisim project exercicio_01.circ as structural Verilog
module main (
  input  [3:0] A4,
  input  [3:0] B4,
  input  C0,
  output out_4,
  output out_5,
  output out_6,
  output out_7,
  output out_8
);

  wire and_1_out, and_2_out, and_3_out, and_4_out, and_5_out, and_6_out, and_7_out, and_8_out, and_9_out,
       and_10_out, and_11_out, and_12_out, and_13_out, and_14_out, or_1_out, or_3_out, or_4_out, xor_1_out,
       xor_2_out, xor_3_out;

  xor xor_1 (xor_1_out, A4[3], A4[3]);
  and and_1 (and_1_out, A4[3], A4[3]);
  and and_2 (and_2_out, A4[3], A4[3]);
  and and_3 (and_3_out, A4[3], A4[3]);
  xor xor_2 (xor_2_out, A4[3], A4[3]);
  xor xor_3 (xor_3_out, A4[3], A4[3]);
  and and_4 (and_4_out, A4[3], A4[3]);
  xor xor_4 (and_1_out, A4[3], A4[3]);
  and and_5 (and_5_out, and_2_out, C0, and_1_out, and_4_out);
  and and_6 (and_6_out, and_1_out, and_1_out, and_4_out);
  and and_7 (and_7_out, xor_1_out, and_4_out);
  and and_8 (and_8_out, C0, and_2_out);
  and and_9 (and_9_out, C0, and_2_out, and_1_out, and_4_out, and_3_out);
  and and_10 (and_10_out, and_1_out, and_1_out, and_4_out, and_3_out);
  and and_11 (and_11_out, xor_1_out, and_4_out, and_3_out, and_3_out);
  and and_12 (and_12_out, xor_3_out, and_3_out);
  and and_13 (and_13_out, C0, and_2_out, and_1_out);
  and and_14 (and_14_out, and_1_out, and_1_out, and_1_out);
  or or_1 (or_1_out, and_13_out, and_14_out, xor_1_out);
  or or_2 (out_4, and_9_out, and_10_out, and_11_out, and_12_out, xor_2_out);
  or or_3 (or_3_out, and_5_out, and_6_out, and_7_out, xor_3_out);
  or or_4 (or_4_out, and_8_out, and_1_out);
  xor xor_5 (out_5, and_3_out, or_3_out);
  xor xor_6 (out_6, and_4_out, or_1_out);
  xor xor_7 (out_7, and_1_out, or_4_out);
  xor xor_8 (out_8, and_2_out, C0);

  assign A4[2:0] = {3{A4[3]}};
  assign B4 = {4{A4[3]}};

  // Notes on the sheet:
  //   P3
  //   G3
  //   P2
  //   G2
  //   P1
  //   G1
  //   P0
  //   G0
  //   c4
  //   s3
  //   s2
  //   s1
endmodule

module full_adder (
  input  Cin,
  input  ln_a,
  input  ln_b,
  output sum,
  output carry
);

  wire and_1_out, and_2_out, xor_1_out;

  and and_1 (and_1_out, ln_a, ln_b);
  xor xor_1 (xor_1_out, ln_a, ln_b);
  and and_2 (and_2_out, xor_1_out, Cin);
  xor xor_2 (sum, Cin, xor_1_out);
  or or_1 (carry, and_2_out, and_1_out);
endmodule

module Carry_look_ahead (
  input  P3,
  input  G3,
  input  P2,
  input  G2,
  input  P1,
  input  G1,
  input  P0,
  input  G0,
  input  C0,
  output out_10,
  output out_11,
  output out_12,
  output out_13
);

  wire and_1_out, and_2_out, and_3_out, and_4_out, and_5_out, and_6_out, and_7_out, and_8_out, and_9_out,
       and_10_out, undriven;

  and and_1 (and_1_out, C0, P0, P1, P2, P3);
  and and_2 (and_2_out, G0, P1, P2, P3);
  and and_3 (and_3_out, G1, P2, P3, undriven, undriven);
  and and_4 (and_4_out, G2, P3);
  and and_5 (and_5_out, C0, P0, P1, P2);
  and and_6 (and_6_out, P1, P1, P2);
  and and_7 (and_7_out, G1, P2);
  and and_8 (and_8_out, C0, P0, P1);
  and and_9 (and_9_out, G0, G0, P1);
  and and_10 (and_10_out, C0, P0);
  or or_1 (out_11, and_5_out, and_6_out, and_7_out, G2);
  or or_2 (out_12, and_8_out, and_9_out, G1);
  or or_3 (out_13, and_10_out, G0);
  or or_4 (out_10, and_1_out, and_2_out, and_3_out, and_4_out, G3);

  // Notes on the sheet:
  //   C1 = G0 + P0C0
  //   C2 = G1 + P1 G0 + P1 P0 C0
  //   C3 = G2 + P2 G1 + P2 P1 G0 + P2 P1 P0 C0
  //   C4 = G3 + P3 G2 + P3 P2 G1 + P3 P2 P1 G0 + P3 P2 P1 P0 C0
endmodule

module adder (
  input  Cin,
  input  [3:0] in_2,
  input  [3:0] in_3,
  output s1,
  output s2,
  output s3,
  output s4,
  output carry
);

  wire full_adder_1_carry, full_adder_2_carry, full_adder_3_carry;

  full_adder full_adder_1 (.Cin(Cin), .ln_a(in_2[0]), .ln_b(in_3[0]), .sum(s1), .carry(full_adder_1_carry));
  full_adder full_adder_2 (
    .Cin(full_adder_1_carry), .ln_a(in_2[1]), .ln_b(in_3[1]), .sum(s2), .carry(full_adder_2_carry));
  full_adder full_adder_3 (
    .Cin(full_adder_2_carry), .ln_a(in_2[2]), .ln_b(in_3[2]), .sum(s3), .carry(full_adder_3_carry));
  full_adder full_adder_4 (.Cin(full_adder_3_carry), .ln_a(in_2[3]), .ln_b(in_3[3]), .sum(s4), .carry(carry));

  // Notes on the sheet:
  //   s0
endmodule

module asdasd (
  input  [3:0] in_1,
  input  [3:0] in_2,
  input  in_3,
  output out_4,
  output out_5,
  output out_6,
  output out_7,
  output out_8
);

  wire and_1_out, and_2_out, and_3_out, and_4_out, carry_look_ahead_1_out_11, carry_look_ahead_1_out_12,
       carry_look_ahead_1_out_13, xor_1_out, xor_2_out, xor_3_out, xor_4_out;

  xor xor_1 (xor_1_out, in_2[3], in_1[3]);
  and and_1 (and_1_out, in_2[3], in_1[3]);
  xor xor_2 (xor_2_out, in_1[2], in_2[2]);
  and and_2 (and_2_out, in_1[2], in_2[2]);
  xor xor_3 (xor_3_out, in_1[1], in_2[1]);
  xor xor_4 (xor_4_out, in_1[0], in_2[0]);
  and and_3 (and_3_out, in_1[1], in_2[1]);
  and and_4 (and_4_out, in_1[0], in_2[0]);
  Carry_look_ahead carry_look_ahead_1 (
    .P3(xor_1_out), .G3(and_1_out), .P2(xor_2_out), .G2(and_2_out), .P1(xor_3_out), .G1(and_3_out),
    .P0(xor_4_out), .G0(and_4_out), .C0(in_3), .out_10(out_4), .out_11(carry_look_ahead_1_out_11),
    .out_12(carry_look_ahead_1_out_12), .out_13(carry_look_ahead_1_out_13));
  xor xor_5 (out_6, xor_2_out, carry_look_ahead_1_out_12);
  xor xor_6 (out_7, xor_3_out, carry_look_ahead_1_out_13);
  xor xor_7 (out_8, xor_4_out, in_3);
  xor xor_8 (out_5, xor_1_out, carry_look_ahead_1_out_11);
endmodule

module resto (
  input  [3:0] in_1,
  input  [3:0] in_2,
  input  in_3
);

  wire asdasd_1_out_5, asdasd_1_out_6, asdasd_1_out_7, n7_segment_display_driver_1_p6,
       n7_segment_display_driver_1_p7, n7_segment_display_driver_1_p8, n7_segment_display_driver_1_p9,
       n7_segment_display_driver_1_p10, n7_segment_display_driver_1_p11, n7_segment_display_driver_1_p12,
       n7_segment_display_driver_2_p3, n7_segment_display_driver_2_p4, n7_segment_display_driver_2_p5,
       n7_segment_display_driver_2_p6, n7_segment_display_driver_2_p7, n7_segment_display_driver_2_p8,
       n7_segment_display_driver_2_p9, n7_segment_display_driver_3_p5, n7_segment_display_driver_3_p6,
       n7_segment_display_driver_3_p7, n7_segment_display_driver_3_p8, n7_segment_display_driver_3_p9,
       n7_segment_display_driver_3_p11;

  // _7_segment_display_driver 7_segment_display_driver_1: pin names not known; wires that end beside it: in_1, in_1[3], in_1[2], in_1[1], in_1[0], n7_segment_display_driver_1_p6, n7_segment_display_driver_1_p7, n7_segment_display_driver_1_p8, n7_segment_display_driver_1_p9, n7_segment_display_driver_1_p10, n7_segment_display_driver_1_p11, n7_segment_display_driver_1_p12
  asdasd asdasd_1 (
    .in_1(in_1), .in_2(in_2), .in_3(in_3), .out_5(asdasd_1_out_5), .out_6(asdasd_1_out_6),
    .out_7(asdasd_1_out_7), .out_8(asdasd_1_out_7));  // open: out_4
  _7_Segment_Display u_7_segment_display_1 (
    .g(n7_segment_display_driver_1_p12), .f(n7_segment_display_driver_1_p11),
    .a(n7_segment_display_driver_1_p6), .b(n7_segment_display_driver_1_p7),
    .e(n7_segment_display_driver_1_p10), .d(n7_segment_display_driver_1_p9),
    .c(n7_segment_display_driver_1_p8));  // open: dp
  _7_Segment_Display u_7_segment_display_2 (
    .g(n7_segment_display_driver_2_p9), .f(n7_segment_display_driver_2_p8),
    .a(n7_segment_display_driver_2_p3), .b(n7_segment_display_driver_2_p4),
    .e(n7_segment_display_driver_2_p7), .d(n7_segment_display_driver_2_p6), .c(n7_segment_display_driver_2_p5));  // open: dp
  // _7_segment_display_driver 7_segment_display_driver_2: pin names not known; wires that end beside it: asdasd_1_out_5, asdasd_1_out_6, n7_segment_display_driver_2_p3, n7_segment_display_driver_2_p4, n7_segment_display_driver_2_p5, n7_segment_display_driver_2_p6, n7_segment_display_driver_2_p7, n7_segment_display_driver_2_p8, n7_segment_display_driver_2_p9
  // _7_segment_display_driver 7_segment_display_driver_3: pin names not known; wires that end beside it: in_2[3], in_2[2], in_2[1], in_2[0], n7_segment_display_driver_3_p5, n7_segment_display_driver_3_p6, n7_segment_display_driver_3_p7, n7_segment_display_driver_3_p8, n7_segment_display_driver_3_p9, n7_segment_display_driver_3_p7, n7_segment_display_driver_3_p11
  _7_Segment_Display u_7_segment_display_3 (
    .g(n7_segment_display_driver_3_p11), .f(n7_segment_display_driver_3_p7),
    .a(n7_segment_display_driver_3_p5), .b(n7_segment_display_driver_3_p6),
    .e(n7_segment_display_driver_3_p9), .d(n7_segment_display_driver_3_p8), .c(n7_segment_display_driver_3_p7));  // open: dp

  // Notes on the sheet:
  //   1 + 2 = 3
endmodule

module mult (
  input  [3:0] in_1,
  input  [3:0] in_2,
  output [7:0] out_3
);

  wire adder_1_cout, adder_1_out, adder_2_cout, adder_2_out, adder_3_cout, adder_4_cout, adder_4_out,
       adder_5_cout, adder_5_out, adder_6_cout, adder_6_out, adder_7_cout, adder_8_cout, adder_9_cout,
       adder_9_out, adder_11_cout, adder_12_cout, and_2_out, and_3_out, and_4_out, and_5_out, and_6_out,
       and_7_out, and_8_out, and_9_out, and_10_out, and_11_out, and_12_out, and_13_out, and_14_out,
       and_15_out, and_16_out;

  and and_1 (out_3[0], in_1[0], in_2[0]);
  and and_2 (and_2_out, in_1[1], in_2[0]);
  and and_3 (and_3_out, in_1[0], in_2[1]);
  and and_4 (and_4_out, in_1[0], in_2[2]);
  and and_5 (and_5_out, in_1[1], in_2[1]);
  and and_6 (and_6_out, in_1[2], in_2[0]);
  and and_7 (and_7_out, in_1[0], in_2[3]);
  and and_8 (and_8_out, in_1[1], in_2[2]);
  and and_9 (and_9_out, in_1[2], in_2[1]);
  and and_10 (and_10_out, in_1[3], in_2[0]);
  and and_11 (and_11_out, in_1[1], in_2[3]);
  and and_12 (and_12_out, in_1[2], in_2[2]);
  and and_13 (and_13_out, in_1[3], in_2[1]);
  and and_14 (and_14_out, in_1[2], in_2[3]);
  and and_15 (and_15_out, in_1[3], in_2[2]);
  and and_16 (and_16_out, in_2[3], in_1[3]);
  Adder #(.width(1)) adder_1 (.a(and_7_out), .b(and_8_out), .out(adder_1_out), .cout(adder_1_cout));  // open: cin
  Adder #(.width(1)) adder_2 (
    .a(and_11_out), .b(and_12_out), .out(adder_2_out), .cin(adder_1_cout), .cout(adder_2_cout));
  Adder #(.width(1)) adder_3 (.a(and_2_out), .b(and_3_out), .out(out_3[1]), .cout(adder_3_cout));  // open: cin
  Adder #(.width(1)) adder_4 (.a(and_4_out), .b(and_5_out), .out(adder_4_out), .cout(adder_4_cout));  // open: cin
  Adder #(.width(1)) adder_5 (
    .a(adder_1_out), .b(and_9_out), .out(adder_5_out), .cin(adder_4_cout), .cout(adder_5_cout));
  Adder #(.width(1)) adder_6 (
    .a(adder_2_out), .b(and_13_out), .out(adder_6_out), .cin(adder_5_cout), .cout(adder_6_cout));
  Adder #(.width(1)) adder_7 (.a(adder_4_out), .b(and_6_out), .out(out_3[2]), .cin(adder_3_cout), .cout(adder_7_cout));
  Adder #(.width(1)) adder_8 (.a(adder_5_out), .b(and_10_out), .out(out_3[3]), .cin(adder_7_cout), .cout(adder_8_cout));
  Adder #(.width(1)) adder_9 (
    .a(and_14_out), .b(and_15_out), .out(adder_9_out), .cin(adder_2_cout), .cout(adder_9_cout));
  Adder #(.width(1)) adder_10 (.a(adder_9_cout), .b(and_16_out), .out(out_3[6]), .cin(adder_12_cout), .cout(out_3[7]));
  Adder #(.width(1)) adder_11 (.a(adder_8_cout), .b(adder_6_out), .out(out_3[4]), .cout(adder_11_cout));  // open: cin
  Adder #(.width(1)) adder_12 (
    .a(adder_6_cout), .b(adder_9_out), .out(out_3[5]), .cin(adder_11_cout), .cout(adder_12_cout));
endmodule
